// Logisim project 4_bit_ALU_stage1.circ as structural Verilog: 1 circuit, main circuit ALU_4bit
// Ci
module ALU_4bit (
  input  in_1,
  input  in_2,
  input  in_3,
  input  X0,
  input  X1,
  input  X2,
  input  X3,
  input  X4,
  input  X5,
  input  X6,
  input  X7,
  input  X8,
  input  X9,
  input  Y0,
  input  Y1,
  input  Y2,
  input  Y3,
  input  Y4,
  input  Y5,
  input  Y6,
  input  Y7,
  input  Y8,
  input  Y9,
  input  ADD,
  input  SUB,
  input  MUL,
  input  DIV,
  input  [1:0] S1S0,
  output s0,
  output s1,
  output s2,
  output s3,
  output A3,
  output A2,
  output Co,
  output A1,
  output A0,
  output B3,
  output B2,
  output B1,
  output B0,
  output OP,
  output P0,
  output P1,
  output P2,
  output P3,
  output P4,
  output P5,
  output P6,
  output MULC
);

  wire and_1_out, and_2_out, and_4_out, and_5_out, and_6_out, and_7_out, and_8_out, and_9_out, and_10_out,
       and_11_out, and_12_out, and_13_out, and_14_out, and_15_out, and_16_out, and_17_out, and_18_out,
       and_19_out, and_20_out, and_21_out, and_22_out, and_23_out, and_24_out, and_25_out, and_26_out,
       and_27_out, and_28_out, and_29_out, and_30_out, and_31_out, and_32_out, and_33_out, and_34_out,
       and_35_out, and_36_out, and_37_out, and_38_out, and_39_out, and_40_out, and_41_out, multiplexer_2_out,
       or_9_out, or_10_out, or_11_out, or_12_out, or_14_out, or_15_out, or_16_out, or_17_out, or_18_out,
       or_19_out, or_20_out, xor_1_out, xor_2_out, xor_4_out, xor_5_out, xor_8_out, xor_9_out, xor_11_out,
       xor_12_out, xor_13_out, xor_14_out, xor_16_out, xor_18_out, xor_19_out, xor_20_out, xor_21_out,
       xor_22_out, xor_24_out, xor_25_out, xor_26_out, xor_28_out;

  Multiplexer #(.select(2)) multiplexer_1 (.in0(ADD), .in1(SUB), .in2(MUL), .in3(DIV), .out(OP), .sel(S1S0));
  or or_1 (A3, X8, X9);
  or or_2 (B3, Y8, Y9);
  or or_3 (A2, X4, X5, X6, X7);
  or or_4 (A1, X6, X7, X2, X3);
  or or_5 (B2, Y4, Y5, Y6, Y7);
  or or_6 (B1, Y6, Y7, Y2, Y3);
  or or_7 (A0, X1, X3, X5, X7, X9);
  or or_8 (B0, Y1, Y3, Y5, Y7, Y9);
  xor xor_1 (xor_1_out, B0, multiplexer_2_out);
  xor xor_2 (xor_2_out, A0, xor_1_out);
  and and_1 (and_1_out, A0, xor_1_out);
  xor xor_3 (s0, multiplexer_2_out, xor_2_out);
  and and_2 (and_2_out, multiplexer_2_out, xor_2_out);
  or or_9 (or_9_out, and_2_out, and_1_out);
  xor xor_4 (xor_4_out, B1, multiplexer_2_out);
  and and_3 (P0, B0, A0);
  xor xor_5 (xor_5_out, A1, xor_4_out);
  and and_4 (and_4_out, A1, xor_4_out);
  and and_5 (and_5_out, A1, B0);
  and and_6 (and_6_out, A0, B1);
  xor xor_6 (s1, or_9_out, xor_5_out);
  and and_7 (and_7_out, or_9_out, xor_5_out);
  xor xor_7 (P1, and_5_out, and_6_out);
  and and_8 (and_8_out, and_5_out, and_6_out);
  or or_10 (or_10_out, and_7_out, and_4_out);
  xor xor_8 (xor_8_out, A2, xor_9_out);
  xor xor_9 (xor_9_out, B2, multiplexer_2_out);
  and and_9 (and_9_out, B0, A2);
  and and_10 (and_10_out, B1, A1);
  and and_11 (and_11_out, B2, A0);
  and and_12 (and_12_out, A2, xor_9_out);
  xor xor_10 (s2, or_10_out, xor_8_out);
  and and_13 (and_13_out, or_10_out, xor_8_out);
  xor xor_11 (xor_11_out, and_10_out, and_11_out);
  and and_14 (and_14_out, and_10_out, and_11_out);
  or or_11 (or_11_out, and_13_out, and_12_out);
  xor xor_12 (xor_12_out, B3, multiplexer_2_out);
  xor xor_13 (xor_13_out, and_9_out, xor_11_out);
  and and_15 (and_15_out, and_9_out, xor_11_out);
  xor xor_14 (xor_14_out, A3, xor_12_out);
  and and_16 (and_16_out, A3, xor_12_out);
  or or_12 (or_12_out, and_15_out, and_14_out);
  xor xor_15 (s3, or_11_out, xor_14_out);
  and and_17 (and_17_out, or_11_out, xor_14_out);
  xor xor_16 (xor_16_out, or_12_out, and_8_out);
  or or_13 (Co, and_17_out, and_16_out);
  and and_18 (and_18_out, or_12_out, and_8_out);
  Multiplexer multiplexer_2 (.in0(in_1), .in1(in_2), .out(multiplexer_2_out), .sel(in_3));
  xor xor_17 (P2, xor_13_out, xor_16_out);
  and and_19 (and_19_out, xor_13_out, xor_16_out);
  or or_14 (or_14_out, and_19_out, and_18_out);
  and and_20 (and_20_out, B0, A3);
  and and_21 (and_21_out, B1, A2);
  and and_22 (and_22_out, B2, A1);
  and and_23 (and_23_out, B3, A0);
  xor xor_18 (xor_18_out, and_22_out, and_23_out);
  and and_24 (and_24_out, and_22_out, and_23_out);
  xor xor_19 (xor_19_out, and_21_out, xor_18_out);
  and and_25 (and_25_out, and_21_out, xor_18_out);
  or or_15 (or_15_out, and_25_out, and_24_out);
  xor xor_20 (xor_20_out, xor_19_out, or_15_out);
  and and_26 (and_26_out, xor_19_out, or_15_out);
  xor xor_21 (xor_21_out, and_20_out, xor_20_out);
  and and_27 (and_27_out, and_20_out, xor_20_out);
  or or_16 (or_16_out, and_27_out, and_26_out);
  xor xor_22 (xor_22_out, xor_21_out, or_16_out);
  and and_28 (and_28_out, xor_21_out, or_16_out);
  xor xor_23 (P3, or_14_out, xor_22_out);
  and and_29 (and_29_out, or_14_out, xor_22_out);
  or or_17 (or_17_out, and_29_out, and_28_out);
  and and_30 (and_30_out, B1, A3);
  and and_31 (and_31_out, B2, A2);
  and and_32 (and_32_out, B3, A1);
  xor xor_24 (xor_24_out, and_31_out, and_32_out);
  and and_33 (and_33_out, and_31_out, and_32_out);
  xor xor_25 (xor_25_out, and_30_out, xor_24_out);
  and and_34 (and_34_out, and_30_out, xor_24_out);
  or or_18 (or_18_out, and_34_out, and_33_out);
  xor xor_26 (xor_26_out, or_18_out, or_17_out);
  and and_35 (and_35_out, or_18_out, or_17_out);
  xor xor_27 (P4, xor_25_out, xor_26_out);
  and and_36 (and_36_out, xor_25_out, xor_26_out);
  or or_19 (or_19_out, and_36_out, and_35_out);
  and and_37 (and_37_out, B3, A2);
  and and_38 (and_38_out, B2, A3);
  xor xor_28 (xor_28_out, and_37_out, and_38_out);
  and and_39 (and_39_out, and_37_out, and_38_out);
  xor xor_29 (P5, or_19_out, xor_28_out);
  and and_40 (and_40_out, or_19_out, xor_28_out);
  or or_20 (or_20_out, and_40_out, and_39_out);
  and and_41 (and_41_out, B3, A3);
  xor xor_30 (P6, and_41_out, or_20_out);
  and and_42 (MULC, and_41_out, or_20_out);

  // Notes on the sheet:
  //   ENCODERS
  //   Ci
  //   4 BIT ADDER SUBTRACTOR
  //   ADD=0 / SUB=1
  //   4 BIT MULTIPLIER
endmodule
