// Logisim project 7_segment_display.circ as structural Verilog: 1 circuit, main circuit 7SEG
module _7SEG (
  input  in_1
);

  wire and_1_out, and_2_out, and_3_out, and_4_out, and_5_out, and_6_out, and_7_out, and_8_out, and_9_out,
       and_10_out, Clock_out, not_1_out, not_2_out, not_3_out, not_4_out, not_5_out, not_6_out, not_7_out,
       not_8_out, not_9_out, not_10_out, or_1_out, or_2_out, or_3_out, or_4_out, or_5_out, or_6_out,
       or_7_out, xnor_1_out, xnor_2_out, xor_1_out;
  wire [3:0] Counter_q;

  xnor xnor_1 (xnor_1_out, Counter_q[2], Counter_q[0]);
  not not_1 (not_1_out, Counter_q[2]);
  not not_2 (not_2_out, Counter_q[1]);
  not not_3 (not_3_out, Counter_q[2]);
  not not_4 (not_4_out, Counter_q[1]);
  not not_5 (not_5_out, Counter_q[0]);
  not not_6 (not_6_out, Counter_q[2]);
  or or_1 (or_1_out, not_6_out, Counter_q[1]);
  not not_7 (not_7_out, Counter_q[0]);
  or or_2 (or_2_out, Counter_q[1], xnor_1_out, Counter_q[3]);
  xnor xnor_2 (xnor_2_out, Counter_q[0], Counter_q[1]);
  or or_3 (or_3_out, Counter_q[2], Counter_q[0], not_2_out);
  and and_1 (and_1_out, or_1_out, not_7_out);
  or or_4 (or_4_out, xnor_2_out, not_1_out);
  and and_2 (and_2_out, not_3_out, not_5_out);
  and and_3 (and_3_out, not_5_out, Counter_q[1]);
  and and_4 (and_4_out, not_3_out, Counter_q[1]);
  and and_5 (and_5_out, Counter_q[2], not_4_out, Counter_q[0]);
  or or_5 (or_5_out, and_2_out, and_3_out, and_4_out, and_5_out);
  _7_Segment_Display u_7_segment_display_1 (
    .g(or_7_out), .f(or_6_out), .a(or_2_out), .b(or_4_out), .e(and_1_out), .d(or_5_out), .c(or_3_out));  // open: dp
  not not_8 (not_8_out, Counter_q[1]);
  not not_9 (not_9_out, Counter_q[0]);
  and and_6 (and_6_out, not_8_out, not_9_out);
  and and_7 (and_7_out, not_8_out, Counter_q[2]);
  and and_8 (and_8_out, not_9_out, Counter_q[2]);
  Clock Clock (.out(Clock_out));
  not not_10 (not_10_out, Counter_q[0]);
  Counter #(.width(4), .max('hf)) Counter (
    .load(in_1), .Q(Counter_q), .clk(Clock_out), .clr(and_9_out));  // open: D, count, carry
  and and_9 (and_9_out, Counter_q[3], Counter_q[1]);
  xor xor_1 (xor_1_out, Counter_q[2], Counter_q[1]);
  and and_10 (and_10_out, Counter_q[1], not_10_out);
  or or_6 (or_6_out, and_6_out, and_7_out, and_8_out, Counter_q[3]);
  or or_7 (or_7_out, xor_1_out, and_10_out, Counter_q[3]);

  // Notes on the sheet:
  //   A
  //   C
  //   E
  //   B
  //   D
  //   F
  //   ABCD
  //   Reset
  //   Reset
endmodule
