// Logisim project PC.circ as structural Verilog: 1 circuit, main circuit Program_counter
module Program_counter (
  input  Set,
  input  Reset,
  input  [3:0] Target,
  input  in_4,
  input  in_5,
  input  in_6,
  output [3:0] PCout
);

  wire and_1_out, and_2_out, and_3_out, and_4_out, and_5_out, and_6_out, and_7_out, and_8_out, clock_1_out,
       or_1_out, or_2_out, or_3_out, or_4_out, xor_1_out, xor_3_out, xor_5_out, xor_7_out;
  wire [3:0] multiplexer_1_out, xor_2_out;

  Clock clock_1 (.out(clock_1_out));
  Multiplexer #(.width(4)) multiplexer_1 (.in0(xor_2_out), .in1(Target), .out(multiplexer_1_out), .sel(in_4));
  D_Flip_Flop d_ff_1 (
    .D(multiplexer_1_out[0]), .clk(clock_1_out), .Q(PCout[0]), .preset(Set), .reset(Reset));  // open: Qn
  D_Flip_Flop d_ff_2 (
    .D(multiplexer_1_out[1]), .clk(clock_1_out), .Q(PCout[1]), .preset(Set), .reset(Reset));  // open: Qn
  D_Flip_Flop d_ff_3 (
    .D(multiplexer_1_out[2]), .clk(clock_1_out), .Q(PCout[2]), .preset(Set), .reset(Reset));  // open: Qn
  xor xor_1 (xor_1_out, PCout[0], in_6);
  and and_1 (and_1_out, PCout[0], in_6);
  D_Flip_Flop d_ff_4 (
    .D(multiplexer_1_out[3]), .clk(clock_1_out), .Q(PCout[3]), .preset(Set), .reset(Reset));  // open: Qn
  and and_2 (and_2_out, in_5, xor_1_out);
  xor xor_2 (xor_2_out[0], in_5, xor_1_out);
  or or_1 (or_1_out, and_2_out, and_1_out);
  xor xor_3 (xor_3_out, PCout[1], in_5);
  and and_3 (and_3_out, PCout[1], in_5);
  xor xor_4 (xor_2_out[1], or_1_out, xor_3_out);
  and and_4 (and_4_out, or_1_out, xor_3_out);
  or or_2 (or_2_out, and_4_out, and_3_out);
  xor xor_5 (xor_5_out, PCout[2], in_5);
  and and_5 (and_5_out, PCout[2], in_5);
  and and_6 (and_6_out, or_2_out, xor_5_out);
  xor xor_6 (xor_2_out[2], or_2_out, xor_5_out);
  or or_3 (or_3_out, and_6_out, and_5_out);
  xor xor_7 (xor_7_out, PCout[3], in_5);
  and and_7 (and_7_out, PCout[3], in_5);
  xor xor_8 (xor_2_out[3], or_3_out, xor_7_out);
  and and_8 (and_8_out, or_3_out, xor_7_out);
  or or_4 (or_4_out, and_8_out, and_7_out);
  // also tied to GND on the sheet: or_4_out

  // Notes on the sheet:
  //   PCin
  //   4 Bit register
  //   PC incrementing circuit
endmodule
